# Fritzing sketch circuit_diagram (saved by Fritzing 0.9.2b)
breadboards: 1

parts:
  D2 = Diode [package=diode-1n4001]
  D4 = Diode [package=diode-1n4001]
  U1 = Voltage Regulator [package=to220-igo]
  Raspberry_Pi_A1 = Raspberry Pi A
  U2 = Voltage Regulator [package=to220-igo]
  R4 = Resistor [tolerance=±5% resistance=220 package="1206 [SMD]"]
  J1 = Basic Servo
  J2 = Basic Servo
  V1 = DC Power [voltage=5]
  P1 = S1133 Si Photodiode [package="8mm Ceramic [THT]"]
  D1 = Diode [package=diode-1n4001]
  D3 = Diode [package=diode-1n4001]
  R5 = Resistor [tolerance=±5% resistance=220 package="1206 [SMD]"]
  P2 = S1133 Si Photodiode [package="8mm Ceramic [THT]"]
  R6 = Resistor [tolerance=±5% resistance=220 package="1206 [SMD]"]
  R7 = Resistor [tolerance=±5% resistance=220 package="1206 [SMD]"]
  P3 = S1133 Si Photodiode [package="8mm Ceramic [THT]"]
  P4 = S1133 Si Photodiode [package="8mm Ceramic [THT]"]

nets:
  N1: D2.A, D1.C
  N2: D2.C, D3.A
  N3: D4.A, D3.C
  GND: D4.C, U1.GND, Raspberry_Pi_A1.GPIO_24, Raspberry_Pi_A1.GPIO_25, Raspberry_Pi_A1.GPIO_8, Raspberry_Pi_A1.GPIO_7, U2.GND, R4.Pin_1, J1.gnd, J2.gnd, P1.cathode, P1.anode, R5.Pin_1, P2.cathode, P2.anode, R6.Pin_1, R7.Pin_1, P3.cathode, P3.anode, P4.cathode, P4.anode
  N4: U1.IN, U2.IN, V1.V-, D1.A
  N5: Raspberry_Pi_A1.GPIO_17, J1.pulse
  N6: Raspberry_Pi_A1.GPIO_4, J2.pulse
  VCC: U2.OUT, J1.vcc, J2.vcc
